// Logisim project mips_cpu_g1.circ as structural Verilog
module main (
);

  IFetch ifetch_1 ();  // open: PCnext, CLK, Reset, PCplus4, instruction
endmodule

module RF (
  input  [1:0] ReadReg1,
  input  [1:0] ReadReg2,
  input  RegWrite,
  input  [1:0] WriteReg,
  input  [31:0] WriteData,
  input  CLK,
  input  Reset,
  output [31:0] ReadData1,
  output [31:0] ReadData2
);

  wire decoder_1_out1, decoder_1_out2, decoder_1_out3;
  wire [31:0] R0_q, R1_q, R2_q, R3_q;

  Decoder #(.select(2)) decoder_1 (
    .out1(decoder_1_out1), .out2(decoder_1_out2), .out3(decoder_1_out3), .sel(WriteReg), .en(RegWrite));  // open: out0
  Register #(.width(32)) R0 (.D(WriteData), .en(1'b0), .clk(CLK), .Q(R0_q), .clr(Reset));
  Register #(.width(32)) R1 (.D(WriteData), .en(decoder_1_out1), .clk(CLK), .Q(R1_q), .clr(Reset));
  Register #(.width(32)) R2 (.D(WriteData), .en(decoder_1_out2), .clk(CLK), .Q(R2_q), .clr(Reset));
  Register #(.width(32)) R3 (.D(WriteData), .en(decoder_1_out3), .clk(CLK), .Q(R3_q), .clr(Reset));
  Multiplexer #(.select(2), .width(32)) multiplexer_1 (
    .in0(R0_q), .in1(R1_q), .in2(R2_q), .in3(R3_q), .out(ReadData1), .sel(ReadReg1));
  Multiplexer #(.select(2), .width(32)) multiplexer_2 (
    .in0(R0_q), .in1(R1_q), .in2(R2_q), .in3(R3_q), .out(ReadData2), .sel(ReadReg2));
endmodule

module IFetch (
  input  [31:0] PCnext,
  input  CLK,
  input  Reset,
  output [31:0] PCplus4,
  output [31:0] instruction
);

  wire [31:0] PCreg_q;

  Register #(.width(32)) PCreg (.D(PCnext), .clk(CLK), .Q(PCreg_q), .clr(Reset));  // open: en
  // Probe on PCreg_q
  Adder #(.width(32)) adder_1 (.a(PCreg_q), .b(32'h4), .out(PCplus4));  // open: cin, cout
  // Probe on PCreg_q[25:2]
  ROM #(.addrWidth(24), .dataWidth(32)) rom_1 (.addr(PCreg_q[25:2]), .data(instruction));

  // Notes on the sheet:
  //   contents of rom_1 (hex, n*v repeats v):
  //   12 24 23 7ae
endmodule

module IBreakdown (
  input  [31:0] Instruction,
  output [5:0] Op,
  output [4:0] rs,
  output [4:0] rt,
  output [4:0] rd,
  output [5:0] shamp,
  output [5:0] funct,
  output [15:0] fmm,
  output [25:0] address
);


  assign Op = Instruction[31:26];
endmodule
